# Fritzing sketch led-pulsante (saved by Fritzing 0.9.3b)
circuit board: 5.90503cm x 2.49166cm
breadboards: 1

parts:
  Componente1 = Arduino Uno (Rev3)
  LED1 = LED - 5mm [color="Red (660nm)" package="5 mm [THT]"]
  R1 = Resistor [tolerance=±5% resistance=220 package=THT]
  R2 = Resistor [tolerance=±5% resistance=1k package=THT]
  S1 = Pushbutton [package="[THT]"]

nets:
  N1: Componente1.D12/MISO, R2.Pin_0, S1.Pin_3, S1.Pin_4
  N2: Componente1.D13/SCK, LED1.anode
  N3: Componente1.GND, R1.Pin_0, R2.Pin_1
  N4: Componente1.5V, S1.Pin_1, S1.Pin_2
  N5: LED1.cathode, R1.Pin_1

// code stored in the sketch: Led con pulsante.ino
// Assegnazione numerica dei pin
int pinBot = 12;
int pinLed = 13;

// Inizializzazione
void setup() {
  // Definizione dei pin
  pinMode(pinBot, INPUT);
  pinMode(pinLed, OUTPUT);
}

// Programma principale
void loop() {
  // Controllo lo stato del pulsante
  if (digitalRead(pinBot) == HIGH) {
    // se premuto accendo il led
    digitalWrite(pinLed, HIGH);
  }
  else {
    // altrimenti lo spengo
    digitalWrite(pinLed, LOW);
  }
}
