# Fritzing sketch potenziometro (saved by Fritzing 0.9.3b)
circuit board: 8.46667cm x 5.64444cm
breadboards: 1

parts:
  R1 = Rotary Potentiometer (Small) [maximum_resistance=100kΩ package=THT]
  M1 = DC Motor
  Componente1 = Arduino Uno (Rev3)

nets:
  N1: R1.leg1, Componente1.5V
  N2: R1.wiper, Componente1.A0
  N3: R1.leg2, M1.pin_2, Componente1.GND
  N4: M1.pin_1, Componente1.D6_PWM

// code stored in the sketch: potenziometro.ino
/********************************************************************
 * Potenziometro.ino                                                *
 *                                                                  *
 * Controllo di un motore in corrente continua                      *
 ********************************************************************/

// Ingresso analogico (campionato a 10 bit)
int analogPin = A0;

// Uscita analogica (campionata a 8 bit)
int motorPin = 6;

// Valore acquisito in ingresso                    
int val = 0;

void setup() {
  // Inizializzazione della porta seriale
  // così da poter vedere i dati acquisiti al computer
  Serial.begin(9600);
  // Il pin del motore è un'uscita
  pinMode(motorPin, OUTPUT);
}

void loop() {
  // Legge la posizione del potenziometro
  val = analogRead(analogPin);
  // Richiede al motore una potenza pari a quella impostata
  // L'uscita è a 8 bit => 2^10 / 2^8 anche oggi fa 4
  analogWrite(motorPin, val/4);
  // Invia il dato anche alla porta seriale (utile in fase di test)
  Serial.println(val);
}
